# Fritzing sketch Circuit Diagram (saved by Fritzing 0.9.3b)
breadboards: 1

parts:
  Arduino_Leonardo = Arduino Leonardo (Rev3b)
  Buzzer = Piezo Speaker
  LCD = LCD1602-I2C
  Blue_LED = LEDs [package=led10mm]
  red_LED = LEDs [package=led10mm]
  SW1 = Pushbutton [package=THT]
  SW2 = Pushbutton [package=THT]
  R1 = Rotary Potentiometer (Small) [maximum_resistance=100kΩ package=THT]

nets:
  N1: Arduino_Leonardo.D2/SDA, Arduino_Leonardo.SDA, LCD.SDA, SW2.leg0
  N2: Arduino_Leonardo.D3_PWM/SCL, Arduino_Leonardo.SCL, LCD.SCL, SW1.leg0
  N3: Arduino_Leonardo.D5_PWM, Buzzer.pin2
  5V: Arduino_Leonardo.5V, LCD.VCC, R1.leg1
  GND: Arduino_Leonardo.GND, LCD.GND, R1.leg2
  N4: Arduino_Leonardo.A0, R1.wiper
  N5: Arduino_Leonardo.D12/A11, Blue_LED.A
  N6: Arduino_Leonardo.D13_PWM, red_LED.A
  N7: Buzzer.pin1, red_LED.C, SW1.leg1, SW2.leg1

custom parts:
  LCD1602-I2C: A standard character display, usually with 2x16 characters. Comes in many colors with LCM1602 IIC attached.
